// Logisim project cpu.circ as structural Verilog
module fetch (
);

  instruction_memory instruction_memory_1 ();  // open: PC, clk, byte_0, byte_1, byte_2, byte_3, byte_4, byte_5, byte_6, byte_7, byte_8, byte_9
endmodule

module instruction_memory (
  input  [63:0] PC,
  input  clk,
  output [7:0] byte_0,
  output [7:0] byte_1,
  output [7:0] byte_2,
  output [7:0] byte_3,
  output [7:0] byte_4,
  output [7:0] byte_5,
  output [7:0] byte_6,
  output [7:0] byte_7,
  output [7:0] byte_8,
  output [7:0] byte_9
);

  Register register_1 ();  // open: D, en, clk, Q, clr
  Adder adder_1 ();  // open: a, b, out, cin, cout
  RAM #(.addrWidth(12)) ram_1 ();  // open: addr, we, oe, clk, din, dout
endmodule
