// Logisim project pc_update.circ as structural Verilog: 2 circuits, main circuit pc_update
module pc_update (
  input  cnd,
  input  [63:0] valC,
  input  [63:0] valM,
  input  [3:0] icode,
  input  [63:0] valP,
  output [63:0] PC
);

  newPC newpc_1 (.cnd(cnd), .valC(valC), .valM(valM), .icode(icode), .valP(valP), .PC(PC));
endmodule

module newPC (
  input  cnd,
  input  [63:0] valC,
  input  [63:0] valM,
  input  [3:0] icode,
  input  [63:0] valP,
  output [63:0] PC
);

  wire [63:0] multiplexer_1_out;

  Multiplexer #(.width(64)) multiplexer_1 (.in0(valP), .in1(valC), .out(multiplexer_1_out), .sel(cnd));
  Multiplexer #(.select(4), .width(64)) multiplexer_2 (
    .in0({64{1'b0}}), .in1(valP), .in2(valP), .in3(valP), .in4(valP), .in5(valP), .in6(valP),
    .in7(multiplexer_1_out), .in10(valP), .in11(valP), .out(PC), .sel(icode));  // open: in8, in9, in12, in13, in14, in15
endmodule
